# Fritzing sketch analog-in (saved by Fritzing 0.9.3b)
breadboards: 1

parts:
  Arduino1 = Arduino Uno (Rev3)
  R4 = Resistor [tolerance=±5% resistance=10k package=THT]
  LED1 = LED - 5mm [color="Red (633nm)" package="5 mm [THT]"]
  LED2 = LED - 5mm [color="Yellow (585nm)" package="5 mm [THT]"]
  LED3 = LED - 5mm [color="Green (555nm)" package="5 mm [THT]"]
  LED4 = LED - 5mm [color="Blue (470nm)" package="5 mm [THT]"]
  U3 = POT [package=3362u]
  R1 = Resistor [tolerance=±1% resistance=220 package=THT]
  R2 = Resistor [tolerance=±1% resistance=220 package=THT]
  R3 = Resistor [tolerance=±1% resistance=220 package=THT]

nets:
  N1: Arduino1.D4, R3.Pin_0
  N2: Arduino1.D5_PWM, R2.Pin_0
  N3: Arduino1.D6_PWM, R1.Pin_0
  N4: Arduino1.D7, R4.Pin_0
  N5: Arduino1.5V, U3.A
  N6: Arduino1.GND, LED1.cathode, LED2.cathode, LED3.cathode, LED4.cathode, U3.E
  N7: R4.Pin_1, LED4.anode
  N8: LED1.anode, R3.Pin_1
  N9: LED2.anode, R2.Pin_1
  N10: LED3.anode, R1.Pin_1
