# Fritzing sketch pwm (saved by Fritzing 0.9.3b)
breadboards: 1

parts:
  LED1 = LED - 5mm [color="Red (633nm)" package="5 mm [THT]"]
  Arduino1 = Arduino Uno (Rev3)
  R1 = Resistor [tolerance=±1% resistance=220 package=THT]

nets:
  N1: LED1.cathode, R1.Pin_1
  N2: LED1.anode, Arduino1.D3_PWM
  N3: Arduino1.GND, R1.Pin_0
